# Fritzing sketch GPIO_test_Blinky (saved by Fritzing 0.9.3b)
breadboards: 2

parts:
  FTDI_to_Serial_Adapter = FTDI Basic Programmer
  ESP8266 = Gizwits WiFi Witty ESP-12F
  JP1 = Header 8 [package=1x08_smd]
  JP2 = Header 8 [package=1x08_smd]
  JP3 = Header 8 [package=1x08_smd]
  IC1 = MCP23S17 [chip_label=MCP23S17 package="DIP (Dual Inline) [THT]"]
  S2 = Pushbutton [package="[THT]"]
  S3 = Pushbutton [package="[THT]"]
  R1 = Resistor [tolerance=±5% resistance=10k package="2512 [SMD]"]
  ADC1 = MCP3208 [package=dil16]
  R2 = Resistor [tolerance=±5% resistance=220 package="2512 [SMD]"]
  LED1 = smd LED [color="Red (633nm)" package="1206 [SMD]"]
  LED2 = smd LED [color="Red (633nm)" package="1206 [SMD]"]
  R3 = Resistor [tolerance=±5% resistance=220 package="2512 [SMD]"]
  LED3 = smd LED [color="Red (633nm)" package="1206 [SMD]"]
  LED4 = smd LED [color="Red (633nm)" package="1206 [SMD]"]
  LED5 = smd LED [color="Red (633nm)" package="1206 [SMD]"]
  LED6 = smd LED [color="Red (633nm)" package="1206 [SMD]"]
  LED7 = smd LED [color="Red (633nm)" package="1206 [SMD]"]
  LED8 = smd LED [color="Red (633nm)" package="1206 [SMD]"]
  R4 = Resistor [tolerance=±5% resistance=220 package="2512 [SMD]"]
  R5 = Resistor [tolerance=±5% resistance=220 package="2512 [SMD]"]
  R6 = Resistor [tolerance=±5% resistance=220 package="2512 [SMD]"]
  R7 = Resistor [tolerance=±5% resistance=220 package="2512 [SMD]"]
  R8 = Resistor [tolerance=±5% resistance=220 package="2512 [SMD]"]
  R9 = Resistor [tolerance=±5% resistance=220 package="2512 [SMD]"]
  LED9 = smd LED [color="Green (565nm)" package="1206 [SMD]"]
  LED10 = smd LED [color="Green (565nm)" package="1206 [SMD]"]
  LED11 = smd LED [color="Green (565nm)" package="1206 [SMD]"]
  LED12 = smd LED [color="Green (565nm)" package="1206 [SMD]"]
  LED14 = smd LED [color="Green (565nm)" package="1206 [SMD]"]
  LED15 = smd LED [color="Green (565nm)" package="1206 [SMD]"]
  LED16 = smd LED [color="Green (565nm)" package="1206 [SMD]"]
  R10 = Resistor [tolerance=±5% resistance=220 package="2512 [SMD]"]
  R11 = Resistor [tolerance=±5% resistance=220 package="2512 [SMD]"]
  R12 = Resistor [tolerance=±5% resistance=220 package="2512 [SMD]"]
  R13 = Resistor [tolerance=±5% resistance=220 package="2512 [SMD]"]
  R14 = Resistor [tolerance=±5% resistance=220 package="2512 [SMD]"]
  R15 = Resistor [tolerance=±5% resistance=220 package="2512 [SMD]"]
  R16 = Resistor [tolerance=±5% resistance=220 package="2512 [SMD]"]
  R17 = Resistor [tolerance=±5% resistance=220 package="2512 [SMD]"]
  LED13 = smd LED [color="Green (565nm)" package="1206 [SMD]"]

nets:
  N1: FTDI_to_Serial_Adapter.RXI, ESP8266.TXD
  N2: FTDI_to_Serial_Adapter.TXO, ESP8266.RXD
  VCC: FTDI_to_Serial_Adapter.POWER, ESP8266.CH_PD, ESP8266.VCC, ESP8266.GPIO2, IC1.pin9, IC1.pin18, S3.Pin_3, S3.Pin_4, R1.Pin_1, ADC1.VREF, ADC1.VDD
  GND: FTDI_to_Serial_Adapter.GND, ESP8266.GND, ESP8266.GPIO15, IC1.pin10, IC1.pin15, IC1.pin16, IC1.pin17, S2.Pin_3, S2.Pin_4, S3.Pin_1, S3.Pin_2, ADC1.DGND, ADC1.AGND, LED1.cathode, LED2.cathode, LED3.cathode, LED4.cathode, LED5.cathode, LED6.cathode, LED7.cathode, LED8.cathode, LED9.cathode, LED10.cathode, LED11.cathode, LED12.cathode, LED14.cathode, LED15.cathode, LED16.cathode, LED13.cathode
  N3: ESP8266.REST, S2.Pin_1, S2.Pin_2
  N4: ESP8266.GPIO16, ADC1.CS/SHDN
  N5: ESP8266.GPIO14, IC1.pin12, ADC1.CLK
  N6: ESP8266.GPIO12, IC1.pin14, ADC1.Dout
  N7: ESP8266.GPIO13, IC1.pin13, ADC1.Din
  N8: ESP8266.GPIO0, R1.Pin_0
  N9: ESP8266.GPIO5, IC1.pin11
  N10: JP1.1, IC1.pin1, R10.Pin_0
  N11: JP1.2, IC1.pin2, R11.Pin_0
  N12: JP1.3, IC1.pin3, R12.Pin_0
  N13: JP1.4, IC1.pin4, R13.Pin_0
  N14: JP1.5, IC1.pin5, R14.Pin_0
  N15: JP1.6, IC1.pin6, R15.Pin_0
  N16: JP1.7, IC1.pin7, R16.Pin_0
  N17: JP1.8, IC1.pin8, R17.Pin_0
  N18: JP2.1, IC1.pin20, IC1.pin28, R9.Pin_1
  N19: JP2.2, IC1.pin19, IC1.pin27, R8.Pin_1
  N20: JP2.3, IC1.pin26, R7.Pin_1
  N21: JP2.4, IC1.pin25, R6.Pin_1
  N22: JP2.5, IC1.pin24, R5.Pin_1
  N23: JP2.6, IC1.pin23, R4.Pin_1
  N24: JP2.7, IC1.pin22, R3.Pin_1
  N25: JP2.8, IC1.pin21, R2.Pin_1
  N26: JP3.1, ADC1.CH0
  N27: JP3.2, ADC1.CH1
  N28: JP3.3, ADC1.CH2
  N29: JP3.4, ADC1.CH3
  N30: JP3.5, ADC1.CH4
  N31: JP3.6, ADC1.CH5
  N32: JP3.7, ADC1.CH6
  N33: JP3.8, ADC1.CH7
  N34: R2.Pin_0, LED2.anode
  N35: LED1.anode, R3.Pin_0
  N36: LED3.anode, R5.Pin_0
  N37: LED4.anode, R4.Pin_0
  N38: LED5.anode, R6.Pin_0
  N39: LED6.anode, R7.Pin_0
  N40: LED7.anode, R8.Pin_0
  N41: LED8.anode, R9.Pin_0
  N42: LED9.anode, R10.Pin_1
  N43: LED10.anode, R11.Pin_1
  N44: LED11.anode, R12.Pin_1
  N45: LED12.anode, R13.Pin_1
  N46: LED14.anode, R15.Pin_1
  N47: LED15.anode, R16.Pin_1
  N48: LED16.anode, R17.Pin_1
  N49: R14.Pin_1, LED13.anode

notes:
  3.3V supply for ESP8266
  MCP3208 and MCP23S17
  GPIO0
  >VCC for normal mode
  >GND for flash mode
  16 GPIO pins
  8 channel A/D converter pins

custom parts:
  MCP23S17: A DIP stand-in part for whatever IC you want. With 28 pins on a 300mil dual inline package (DIP) footprint.
