# Fritzing sketch Clouduino_Webserver_LEDs_fritzing (saved by Fritzing 0.9.3b)
breadboards: 2

parts:
  FTDI_to_Serial_Adapter = FTDI Basic Programmer
  ESP8266 = Gizwits WiFi Witty ESP-12F
  JP1 = Header 8 [package=1x08_smd]
  JP2 = Header 8 [package=1x08_smd]
  JP3 = Header 8 [package=1x08_smd]
  IC1 = MCP23S17 [chip_label=MCP23S17 package="DIP (Dual Inline) [THT]"]
  S2 = Pushbutton [package="[THT]"]
  S3 = Pushbutton [package="[THT]"]
  R1 = Resistor [tolerance=±5% resistance=10k package="2512 [SMD]"]
  ADC1 = MCP3208 [package=dil16]
  R2 = Resistor [tolerance=±5% resistance=220 package="2512 [SMD]"]
  LED1 = smd LED [color="Red (633nm)" package="1206 [SMD]"]
  LED2 = smd LED [color="Red (633nm)" package="1206 [SMD]"]
  R3 = Resistor [tolerance=±5% resistance=220 package="2512 [SMD]"]

nets:
  N1: FTDI_to_Serial_Adapter.RXI, ESP8266.TXD
  N2: FTDI_to_Serial_Adapter.TXO, ESP8266.RXD
  VCC: FTDI_to_Serial_Adapter.POWER, ESP8266.CH_PD, ESP8266.VCC, ESP8266.GPIO2, IC1.pin9, IC1.pin18, S3.Pin_3, S3.Pin_4, R1.Pin_1, ADC1.VREF, ADC1.VDD
  GND: FTDI_to_Serial_Adapter.GND, ESP8266.GND, ESP8266.GPIO15, IC1.pin10, IC1.pin15, IC1.pin16, IC1.pin17, S2.Pin_3, S2.Pin_4, S3.Pin_1, S3.Pin_2, ADC1.DGND, ADC1.AGND, LED1.cathode, LED2.cathode
  N3: ESP8266.REST, S2.Pin_1, S2.Pin_2
  N4: ESP8266.GPIO16, ADC1.CS/SHDN
  N5: ESP8266.GPIO14, IC1.pin12, ADC1.CLK
  N6: ESP8266.GPIO12, IC1.pin14, ADC1.Dout
  N7: ESP8266.GPIO13, IC1.pin13, ADC1.Din
  N8: ESP8266.GPIO0, R1.Pin_0
  N9: ESP8266.GPIO5, IC1.pin11
  N10: JP1.1, IC1.pin1
  N11: JP1.2, IC1.pin2
  N12: JP1.3, IC1.pin3
  N13: JP1.4, IC1.pin4
  N14: JP1.5, IC1.pin5
  N15: JP1.6, IC1.pin6
  N16: JP1.7, IC1.pin7
  N17: JP1.8, IC1.pin8
  N18: JP2.1, IC1.pin20, IC1.pin28
  N19: JP2.2, IC1.pin19, IC1.pin27
  N20: JP2.3, IC1.pin26
  N21: JP2.4, IC1.pin25
  N22: JP2.5, IC1.pin24
  N23: JP2.6, IC1.pin23
  N24: JP2.7, IC1.pin22, R3.Pin_1
  N25: JP2.8, IC1.pin21, R2.Pin_1
  N26: JP3.1, ADC1.CH0
  N27: JP3.2, ADC1.CH1
  N28: JP3.3, ADC1.CH2
  N29: JP3.4, ADC1.CH3
  N30: JP3.5, ADC1.CH4
  N31: JP3.6, ADC1.CH5
  N32: JP3.7, ADC1.CH6
  N33: JP3.8, ADC1.CH7
  N34: R2.Pin_0, LED1.anode
  N35: LED2.anode, R3.Pin_0

notes:
  3.3V supply for ESP8266
  MCP3208 and MCP23S17
  GPIO0
  >VCC for normal mode
  >GND for flash mode
  16 GPIO pins
  8 channel A/D converter pins

custom parts:
  MCP23S17: A DIP stand-in part for whatever IC you want. With 28 pins on a 300mil dual inline package (DIP) footprint.
